# Fritzing sketch CoffeeAssist (saved by Fritzing 0.9.3b)

parts:
  Raspberry_Pi_1 = Raspberry Pi 3 [part_number=RPI-3-V1.2]
  元件1 = HX711 Weighing Sensor Module
  LCM1602_IIC2 = LCM1602 IIC [part_number="LCM1602 IIC" chip_label="LCM1602 IIC" package="DIP (Dual Inline) [THT]"]
  LCD4 = LCD screen
  R1 = BBC MicroBit

nets:
  N1: Raspberry_Pi_1.GPIO2, LCM1602_IIC2.SDA
  N2: Raspberry_Pi_1.GPIO3, LCM1602_IIC2.SCL
  GND: Raspberry_Pi_1.GND, 元件1.GND, LCM1602_IIC2.GND
  N3: Raspberry_Pi_1.GIPO17, R1.P0_ANALOG_IN
  N4: Raspberry_Pi_1.GIPO27, R1.P1_ANALOG_IN
  N5: Raspberry_Pi_1.GIPO5, 元件1.DO/RX
  N6: Raspberry_Pi_1.GIPO6, 元件1.CK/TX
  VCC: Raspberry_Pi_1.5V, 元件1.VCC, LCM1602_IIC2.VCC
  N7: LCM1602_IIC2.E, LCD4.E
  N8: LCM1602_IIC2.D0, LCD4.DB0
  N9: LCM1602_IIC2.D1, LCD4.DB1
  N10: LCM1602_IIC2.D2, LCD4.DB2
  N11: LCM1602_IIC2.D3, LCD4.DB3
  N12: LCM1602_IIC2.D4, LCD4.DB4
  N13: LCM1602_IIC2.D5, LCD4.DB5
  N14: LCM1602_IIC2.D6, LCD4.DB6
  N15: LCM1602_IIC2.D7, LCD4.DB7
  N16: LCM1602_IIC2.A, LCD4.LED+
  N17: LCM1602_IIC2.K, LCD4.LED-
  N18: LCM1602_IIC2.LED_A, LCM1602_IIC2.LED_B

custom parts:
  LCM1602 IIC: I2C-Module to use a 1602 or 2004 LCD on with the wire.h libory Serial LCD Modul
  BBC MicroBit: The BBC MICRO:BIT
